# Fritzing sketch Motor Fritz (saved by Fritzing 0.9.2b)
breadboards: 1

parts:
  Part1 = Arduino Uno (Rev3)  # not connected
  Part2 = 2A MOTOR SHIELD 9
  M1 = DC Motor
  M2 = DC Motor
  Part3 = Bluetooth HC-06  # not connected

nets:
  N1: Part2.M2+, M2.pin_1
  N2: Part2.M2-, M2.pin_2
  N3: Part2.M1+, M1.pin_1
  N4: Part2.M1-, M1.pin_2
