# Fritzing sketch optical sensor (saved by Fritzing 0.9.2b)
breadboards: 1

parts:
  TCRT1 = TCRT5000 sensor module [part_number=151608]  # not connected
  TCRT2 = TCRT5000 sensor module [part_number=151608]  # not connected
  R2 = Resistor [tolerance=±5% resistance=100 package=THT]
  R3 = Resistor [tolerance=±5% resistance=100 package=THT]
  R4 = Resistor [tolerance=±5% resistance=10k package=THT]
  R1 = Resistor [tolerance=±5% resistance=10k package="2512 [SMD]"]
  부품1 = Arduino Uno (Rev3)

nets:
  N1: R2.Pin_1, R3.Pin_0, R4.Pin_0, R1.Pin_1, 부품1.5V
  N2: R4.Pin_1, 부품1.A5/SCL
  N3: R1.Pin_0, 부품1.A0

custom parts:
  TCRT5000 sensor module: breakout board with TCRT5000
